# Fritzing sketch schematic (saved by Fritzing 0.9.3b)
breadboards: 1

parts:
  U1 = attiny85 [package=dip]
  LED1 = LED - 5mm [color="Blue (525nm)" package="5 mm [THT]"]
  LED2 = LED - 5mm [color="Green (560nm)" package="5 mm [THT]"]
  LED3 = LED - 5mm [color="Red (633nm)" package="5 mm [THT]"]
  R1 = Resistor [tolerance=±5% resistance=100 package=THT]
  R2 = Resistor [tolerance=±5% resistance=100 package=THT]
  R3 = Resistor [tolerance=±5% resistance=100 package=THT]
  S1 = Tilt Switch [package=THT]
  BAT1 = Battery Holders [package=battcon_12mm]

nets:
  N1: U1.Pin_3, S1.Pin_2
  GND: U1.Pin_4, R1.Pin_1, R2.Pin_1, R3.Pin_1, S1.Pin_1, BAT1.-
  N2: U1.Pin_5, LED2.anode
  N3: U1.Pin_6, LED3.anode
  N4: U1.Pin_7, LED1.anode
  3V: U1.Pin_8, BAT1.+
  N5: LED1.cathode, R2.Pin_0
  N6: LED2.cathode, R3.Pin_0
  N7: LED3.cathode, R1.Pin_0
